# Fritzing sketch ir (saved by Fritzing 0.9.3b)
breadboards: 1

parts:
  U2 = ESP8266 WiFi Module [part_number=ESP8266]
  R4 = Resistor [tolerance=±1% resistance=220 package=THT]
  R5 = Resistor [tolerance=±1% resistance=10k package=THT]
  C1 = Electrolytic Capacitor [capacitance=100µF voltage=16V package="100 mil [THT, electrolytic]"]
  R7 = Resistor [tolerance=±1% resistance=10k package=THT]
  R8 = Resistor [tolerance=±1% resistance=10k package=THT]
  R9 = Resistor [tolerance=±1% resistance=10k package=THT]
  R10 = Resistor [tolerance=±1% resistance=10k package=THT]
  R11 = Resistor [tolerance=±1% resistance=10k package=THT]
  V1 = DC Power [voltage=3.3V]
  R15 = Resistor [tolerance=±1% resistance=18 package=THT]
  LED = LED - 3mm [color="Green (565nm)" package="3 mm [THT]"]
  C3 = Capacitor [package=cap-pth-small2]
  D1 = LTE-302 [package=lte-302]
  Q1 = TRANSISTOR_NPN [package=to-92]
  R16 = Resistor [tolerance=±1% resistance=1k package=THT]

nets:
  N1: U2.VCC, R5.Pin_0, C1.+, R7.Pin_0, R8.Pin_0, R9.Pin_0, R11.Pin_0, V1.V+, R15.Pin_0, C3.1
  N2: U2.GPIO_0, R7.Pin_1
  N3: U2.GPIO_2, R8.Pin_1
  N4: U2.CH_PD, R9.Pin_1
  N5: U2.GND, R4.Pin_1, C1.-, R10.Pin_1, V1.V-, C3.2, Q1.E
  N6: U2.GPIO_15, R10.Pin_0
  N7: U2.GPIO_4, LED.anode
  N8: U2.GPIO_5, R11.Pin_1
  N9: U2.GPIO_13, R16.Pin_0
  N10: U2.REST, R5.Pin_1
  N11: R4.Pin_0, LED.cathode
  N12: R15.Pin_1, D1.A
  N13: D1.C, Q1.C
  N14: Q1.B, R16.Pin_1
